// Digital circuit address_decoding.dig as structural Verilog
module address_decoding (
  input  AS,
  input  A20,
  input  A21,
  input  A22,
  input  A23,
  input  LDS,
  input  UDS,
  input  RW,
  output CSROM,
  output CSRAM0,
  output CSDUART,
  output LOW_READ,
  output LOW_WRITE,
  output UPPER_READ,
  output UPPER_WRITE,
  output nASOUT,
  output nRWOUT,
  output nUDSOUT,
  output nLDSOUT
);

  wire and_1_out, and_2_out, and_3_out, and_4_out, and_5_out, and_6_out, and_7_out, and_8_out, and_9_out,
       and_10_out, and_11_out, not_1_out, not_2_out, not_3_out, not_4_out, not_5_out, not_6_out;

  not not_1 (not_1_out, A20);
  not not_2 (not_2_out, A21);
  not not_3 (not_3_out, A22);
  not not_4 (not_4_out, A23);
  not not_5 (not_5_out, UDS);
  not not_6 (not_6_out, RW);
  and and_1 (and_1_out, LDS, UDS);
  and and_2 (and_2_out, LDS, UDS);
  or or_1 (CSDUART, not_1_out, not_2_out, not_3_out, not_4_out, AS, LDS, not_5_out);
  and and_3 (and_3_out, not_1_out, A23);
  and and_4 (and_4_out, A21, not_4_out);
  and and_5 (and_5_out, not_2_out, A22);
  and and_6 (and_6_out, not_3_out, A23);
  and and_7 (and_7_out, A23, not_5_out);
  and and_8 (and_8_out, A21, not_4_out);
  and and_9 (and_9_out, not_2_out, A22);
  and and_10 (and_10_out, not_3_out, A23);
  and and_11 (and_11_out, A23, not_5_out);
  or or_2 (UPPER_READ, A21, A22, A23, AS, not_6_out, UDS);
  or or_3 (UPPER_WRITE, not_1_out, A21, A22, A23, AS, RW, UDS);
  or or_4 (CSROM, A20, A21, A22, A23, AS, and_1_out, not_6_out);
  or or_5 (CSRAM0, not_1_out, A21, A22, A23, AS, and_2_out);
  or or_6 (LOW_READ, and_3_out, and_4_out, and_5_out, and_6_out, and_7_out, AS, LDS, not_6_out);
  or or_7 (LOW_WRITE, not_1_out, and_8_out, and_9_out, and_10_out, and_11_out, AS, LDS, RW);

  assign nASOUT = AS;
  assign nLDSOUT = LDS;
  assign nRWOUT = RW;
  assign nUDSOUT = UDS;

  // Notes on the sheet:
  //   nASOUT: pin 20
  //   nRWOUT: pin 23
  //   nUDSOUT: pin 21
  //   nLDSOUT: pin 22
endmodule
