// Digital circuit address_decoding_v2.dig as structural Verilog
module address_decoding_v2 (
  input  AS,
  input  A20,
  input  A21,
  input  A22,
  input  A23,
  input  nUDS,
  input  nLDS,
  input  R_nW,
  input  A16,
  input  A17,
  input  A18,
  input  A19,
  output CSROM,
  output ODDREAD,
  output ODDWRITE,
  output EVENREAD,
  output EVENWRITE,
  output CSRAM0,
  output DUARTSEL,
  output AS_2
);

  wire and_1_out, not_2_out, not_3_out, not_4_out, not_5_out, not_6_out, not_7_out;

  and and_1 (and_1_out, A16, A17, A18, A19);
  not not_1 (AS_2, AS);
  not not_2 (not_2_out, A20);
  not not_3 (not_3_out, A21);
  not not_4 (not_4_out, A22);
  not not_5 (not_5_out, A23);
  not not_6 (not_6_out, nUDS);
  not not_7 (not_7_out, nLDS);
  nand nand_1 (CSROM, AS_2, not_2_out, not_3_out, not_4_out, not_5_out);
  nand nand_2 (CSRAM0, AS_2, not_5_out, not_3_out, not_4_out, A20);
  nand nand_3 (DUARTSEL, A20, not_3_out, A22, AS_2, A23, and_1_out);
  nand nand_4 (EVENREAD, not_6_out, AS_2, R_nW);
  nand nand_5 (ODDREAD, R_nW, AS_2, not_7_out);
  nand nand_6 (EVENWRITE, CSROM, EVENREAD, AS_2, not_6_out);
  nand nand_7 (ODDWRITE, CSROM, ODDREAD, AS_2, not_7_out);

  // Notes on the sheet:
  //   CSROM: pin 15
  //   AS: pin 6
  //   A20: pin 2
  //   A21: pin 3
  //   A22: pin 4
  //   A23: pin 5
  //   ODDREAD: pin 18
  //   ODDWRITE: pin 19
  //   EVENREAD: pin 20
  //   EVENWRITE: pin 21
  //   CSRAM0: pin 16
  //   DUARTSEL: pin 17
  //   nUDS: pin 9
  //   nLDS: pin 7
  //   R_nW: pin 8
  //   A16: pin 10
  //   A17: pin 11
  //   A18: pin 13
  //   A19: pin 14
  //   AS_2: pin 22
  //   AS output is used for bus error triggering
endmodule
