// Digital circuit deciding.dig as structural Verilog
module deciding (
  input  A20,
  input  A21,
  input  A22,
  input  A23,
  input  LDS,
  input  UDS,
  output CS_Mem_1_Even,
  output CS_Mem_1_Odd
);

  or or_1 (CS_Mem_1_Even, A20, A21, A22, A23, LDS);
  or or_2 (CS_Mem_1_Odd, CS_Mem_1_Even, UDS);
endmodule
