// Digital circuit decoding.dig as structural Verilog
module decoding (
  input  nUDS,
  input  nLDS,
  input  R_nW,
  input  nAS,
  input  A1,
  input  A2,
  input  A3,
  input  A4,
  input  A5,
  input  A6,
  input  A7,
  input  A8,
  input  A9,
  input  A10,
  input  A11,
  input  A12,
  input  A13,
  input  A14,
  input  A15,
  input  A16,
  output UPPER_WRITE,
  output out_6,
  output UPPER_READ,
  output out_8,
  output LOWER_WRITE,
  output out_10,
  output LOWER_READ,
  output out_12,
  output D1,
  output D2,
  output D3,
  output D4,
  output D5,
  output D6,
  output D7,
  output D8,
  output D9,
  output D10,
  output D11,
  output D12,
  output D13,
  output D14,
  output D15,
  output D16
);

  _74139 _74139_1 (
    .pin1(nLDS), .pin2(nAS), .pin3(R_nW), .pin4(LOWER_WRITE), .pin5(out_10), .pin6(LOWER_READ),
    .pin7(out_12), .pin8(1'b0), .pin9(out_8), .pin10(UPPER_READ), .pin11(out_6), .pin12(UPPER_WRITE),
    .pin13(R_nW), .pin14(nAS), .pin15(nUDS), .pin16(1'b1));
  // _28c512 _28c512_1: pin names not known; wires that end beside it: A16, A13, A8, A7, A6, A5, A4, A3, A2, A1, D1, D2, D3, 1'b0, 1'b1, LOWER_WRITE, A15, A14, A9, A10, A12, LOWER_READ, A11
  // _28c512 _28c512_2: pin names not known; wires that end beside it: A16, A13, A8, A7, A6, A5, A4, A3, A2, A1, D9, D10, D11, 1'b0, 1'b1, UPPER_WRITE, A15, A14, A9, A10, A12, UPPER_READ, A11
endmodule
