// Digital circuit decoding2.dig as structural Verilog
module decoding2 (
  input  nUDS,
  input  nLDS,
  input  R_nW,
  input  nAS,
  input  A1,
  input  A2,
  input  A3,
  input  A4,
  input  A5,
  input  A6,
  input  A7,
  input  A8,
  input  A9,
  input  A10,
  input  A11,
  input  A12,
  input  A13,
  input  A14,
  input  A15,
  input  A16,
  input  A17,
  input  A18,
  input  A19,
  input  A20,
  input  A21,
  input  A22,
  input  A23,
  input  in_60,
  output UPPER_WRITE,
  output out_6,
  output UPPER_READ,
  output out_8,
  output LOWER_WRITE,
  output out_10,
  output LOWER_READ,
  output out_12,
  output D0,
  output D1,
  output D2,
  output D3,
  output D4,
  output D5,
  output D6,
  output D7,
  output D8,
  output D9,
  output D10,
  output D11,
  output D12,
  output D13,
  output D14,
  output D15,
  output out_52,
  output out_53,
  output out_54,
  output out_55,
  output out_56,
  output out_57,
  output out_58,
  output out_59
);

  wire not_1_out;

  not not_1 (not_1_out, A23);
  _74139 _74139_1 (
    .pin1(nLDS), .pin2(nAS), .pin3(R_nW), .pin4(LOWER_WRITE), .pin5(out_10), .pin6(LOWER_READ),
    .pin7(out_12), .pin8(1'b0), .pin9(out_8), .pin10(UPPER_READ), .pin11(out_6), .pin12(UPPER_WRITE),
    .pin13(R_nW), .pin14(nAS), .pin15(nUDS), .pin16(1'b1));
  EEPROM #(.AddrBits(19), .isProgramMemory("true"), .Bits(8)) Lower_ROM (
    .A({A19, A18, A17, A16, A15, A14, A13, A12, A11, A10, A9, A8, A7, A6, A5, A4, A3, A2, A1}),
    .CS(~not_1_out), .WE(~1'b1), .OE(~LOWER_READ), .D({D7, D6, D5, D4, D3, D2, D1, D0}));
  EEPROM #(.AddrBits(19), .isProgramMemory("true"), .Bits(8)) Upper_ROM (
    .A({A19, A18, A17, A16, A15, A14, A13, A12, A11, A10, A9, A8, A7, A6, A5, A4, A3, A2, A1}),
    .CS(~not_1_out), .WE(~1'b1), .OE(~UPPER_READ), .D({D15, D14, D13, D12, D11, D10, D9, D8}));
  RAMSinglePortSel #(.AddrBits(19), .Bits(8)) Bank_0_Lower (
    .A({A19, A18, A17, A16, A15, A14, A13, A12, A11, A10, A9, A8, A7, A6, A5, A4, A3, A2, A1}), .CS(~out_52),
    .WE(~LOWER_WRITE), .OE(~LOWER_READ), .D({D7, D6, D5, D4, D3, D2, D1, D0}));
  RAMSinglePortSel #(.AddrBits(19), .Bits(8)) Bank_0_Upper (
    .A({A19, A18, A17, A16, A15, A14, A13, A12, A11, A10, A9, A8, A7, A6, A5, A4, A3, A2, A1}), .CS(~out_52),
    .WE(~UPPER_WRITE), .OE(~UPPER_READ), .D({D15, D14, D13, D12, D11, D10, D9, D8}));
  _74138 _74138_1 (
    .pin1(A20), .pin2(A21), .pin3(A22), .pin4(A23), .pin5(nAS), .pin6(in_60), .pin7(out_59), .pin8(1'b0),
    .pin9(out_58), .pin10(out_57), .pin11(out_56), .pin12(out_55), .pin13(out_54), .pin14(out_53),
    .pin15(out_52), .pin16(1'b1));
  RAMSinglePortSel #(.AddrBits(19), .Bits(8)) Bank_1_Lower (
    .A({A19, A18, A17, A16, A15, A14, A13, A12, A11, A10, A9, A8, A7, A6, A5, A4, A3, A2, A1}), .CS(~out_53),
    .WE(~LOWER_WRITE), .OE(~LOWER_READ), .D({D7, D6, D5, D4, D3, D2, D1, D0}));
  RAMSinglePortSel #(.AddrBits(19), .Bits(8)) Bank_1_Upper (
    .A({A19, A18, A17, A16, A15, A14, A13, A12, A11, A10, A9, A8, A7, A6, A5, A4, A3, A2, A1}), .CS(~out_53),
    .WE(~UPPER_WRITE), .OE(~UPPER_READ), .D({D15, D14, D13, D12, D11, D10, D9, D8}));
  RAMSinglePortSel #(.AddrBits(19), .Bits(8)) Bank_2_Lower (
    .A({A19, A18, A17, A16, A15, A14, A13, A12, A11, A10, A9, A8, A7, A6, A5, A4, A3, A2, A1}), .CS(~out_54),
    .WE(~LOWER_WRITE), .OE(~LOWER_READ), .D({D7, D6, D5, D4, D3, D2, D1, D0}));
  RAMSinglePortSel #(.AddrBits(19), .Bits(8)) Bank_1_Upper_2 (
    .A({A19, A18, A17, A16, A15, A14, A13, A12, A11, A10, A9, A8, A7, A6, A5, A4, A3, A2, A1}), .CS(~out_54),
    .WE(~UPPER_WRITE), .OE(~UPPER_READ), .D({D15, D14, D13, D12, D11, D10, D9, D8}));
  RAMSinglePortSel #(.AddrBits(19), .Bits(8)) Bank_3_Lower (
    .A({A19, A18, A17, A16, A15, A14, A13, A12, A11, A10, A9, A8, A7, A6, A5, A4, A3, A2, A1}), .CS(~out_55),
    .WE(~LOWER_WRITE), .OE(~LOWER_READ), .D({D7, D6, D5, D4, D3, D2, D1, D0}));
  RAMSinglePortSel #(.AddrBits(19), .Bits(8)) Bank_1_Upper_3 (
    .A({A19, A18, A17, A16, A15, A14, A13, A12, A11, A10, A9, A8, A7, A6, A5, A4, A3, A2, A1}), .CS(~out_55),
    .WE(~UPPER_WRITE), .OE(~UPPER_READ), .D({D15, D14, D13, D12, D11, D10, D9, D8}));

  // Notes on the sheet:
  //   in_60: default 1
endmodule
