// Digital circuit dtack_circuit.dig as structural Verilog
module dtack_circuit (
  input  nROMSEL,
  input  nRAM0SEL,
  input  nDUARTDTACK,
  input  nBUSDTACK,
  input  nIRQ1,
  input  nIRQ2,
  input  nIRQ3,
  input  nIRQ4,
  input  nIRQ5,
  input  nIRQ6,
  input  nIRQ7,
  output nDTACK,
  output IPL0,
  output IPL1,
  output IPL2
);

  wire nand_1_out, not_1_out, not_2_out, not_3_out, not_4_out, not_5_out, not_6_out, not_7_out, not_8_out,
       notconnected_1_out;

  // NotConnected on notconnected_1_out
  nand nand_1 (nand_1_out, nROMSEL, nRAM0SEL, nDUARTDTACK, nBUSDTACK);
  not not_1 (not_1_out, notconnected_1_out);
  not not_2 (not_2_out, nIRQ1);
  not not_3 (not_3_out, nIRQ2);
  not not_4 (not_4_out, nIRQ3);
  not not_5 (not_5_out, nIRQ4);
  not not_6 (not_6_out, nIRQ5);
  not not_7 (not_7_out, nIRQ6);
  not not_8 (not_8_out, nIRQ7);
  PriorityEncoder #(.Selector_Bits(3)) priorityencoder_1 (
    .in0(not_1_out), .in1(not_2_out), .in2(not_3_out), .in3(not_4_out), .in4(not_5_out), .in5(not_6_out),
    .in6(not_7_out), .in7(not_8_out), .num({IPL2, IPL1, IPL0}));  // open: any
  not not_9 (nDTACK, nand_1_out);

  // Notes on the sheet:
  //   nROMSEL: pin 4
  //   nRAM0SEL: pin 3
  //   nDUARTDTACK: pin 2
  //   nDTACK: pin 17
  //   nBUSDTACK: pin 5
  //   IPL0: pin 14
  //   nIRQ1: pin 6
  //   nIRQ2: pin 7
  //   nIRQ3: pin 8
  //   nIRQ4: pin 9
  //   nIRQ5: pin 10
  //   nIRQ6: pin 11
  //   nIRQ7: pin 13
  //   IPL1: pin 15
  //   IPL2: pin 16
endmodule
