// Digital circuit iack_glue_logic.dig as structural Verilog
module iack_glue_logic (
  input  A1,
  input  A2,
  input  A3,
  input  nAS,
  input  FC0,
  input  FC1,
  input  FC2,
  output nIACK5,
  output nIACK3,
  output nIACK4,
  output nIACK1,
  output nIACK2,
  output nIACK7,
  output nIACK6,
  output nIACK0
);

  wire and_1_out, and_2_out, decoder_1_out_0, decoder_1_out_1, decoder_1_out_2, decoder_1_out_3,
       decoder_1_out_4, decoder_1_out_5, decoder_1_out_6, decoder_1_out_7, not_1_out;
  wire [2:0] and_4_out;

  and and_1 (and_1_out, FC0, FC1, FC2);
  not not_1 (not_1_out, nAS);
  and and_2 (and_2_out, and_1_out, not_1_out);
  and and_3 (and_4_out[0], and_2_out, A1);
  and and_4 (and_4_out[1], and_2_out, A2);
  and and_5 (and_4_out[2], and_2_out, A3);
  Decoder #(.Selector_Bits(3)) decoder_1 (
    .sel(and_4_out), .out_0(decoder_1_out_0), .out_1(decoder_1_out_1), .out_2(decoder_1_out_2),
    .out_3(decoder_1_out_3), .out_4(decoder_1_out_4), .out_5(decoder_1_out_5), .out_6(decoder_1_out_6),
    .out_7(decoder_1_out_7));
  not not_2 (nIACK0, decoder_1_out_0);
  not not_3 (nIACK1, decoder_1_out_1);
  not not_4 (nIACK2, decoder_1_out_2);
  not not_5 (nIACK3, decoder_1_out_3);
  not not_6 (nIACK4, decoder_1_out_4);
  not not_7 (nIACK5, decoder_1_out_5);
  not not_8 (nIACK6, decoder_1_out_6);
  not not_9 (nIACK7, decoder_1_out_7);

  // Notes on the sheet:
  //   A1: pin 5
  //   A2: pin 6
  //   A3: pin 7
  //   nAS: pin 8
  //   FC0: pin 2
  //   FC1: pin 3
  //   FC2: pin 4
  //   nIACK5: pin 19
  //   nIACK3: pin 17
  //   nIACK4: pin 18
  //   nIACK1: pin 15
  //   nIACK2: pin 16
  //   nIACK7: pin 21
  //   nIACK6: pin 20
  //   nIACK0: pin 14
endmodule
