// Digital circuit irq_glue_logic.dig as structural Verilog
module irq_glue_logic (
  input  A1,
  input  A2,
  input  A3,
  input  nAS,
  input  FC0,
  input  FC1,
  input  FC2,
  input  IRQ1,
  input  IRQ2,
  input  IRQ3,
  input  IRQ4,
  input  IRQ5,
  input  IRQ6,
  input  IRQ7,
  output IACK5,
  output IACK3,
  output IACK4,
  output IACK1,
  output IACK2,
  output IACK7,
  output IACK6,
  output IPL0,
  output IPL1,
  output IPL2,
  output IACK0
);

  wire _74138_1_pin5, not_1_out, not_2_out, not_3_out, not_4_out, not_5_out, not_6_out, not_7_out, not_8_out,
       notconnected_1_out;

  // NotConnected on notconnected_1_out
  _74138 _74138_1 (
    .pin1(A1), .pin2(A2), .pin3(A3), .pin4(nAS), .pin5(_74138_1_pin5), .pin6(1'b1), .pin7(IACK7),
    .pin8(1'b0), .pin9(IACK6), .pin10(IACK5), .pin11(IACK4), .pin12(IACK3), .pin13(IACK2), .pin14(IACK1),
    .pin15(IACK0), .pin16(1'b1));
  not not_1 (not_1_out, notconnected_1_out);
  not not_2 (not_2_out, IRQ1);
  not not_3 (not_3_out, IRQ2);
  not not_4 (not_4_out, IRQ3);
  not not_5 (not_5_out, IRQ4);
  not not_6 (not_6_out, IRQ5);
  not not_7 (not_7_out, IRQ6);
  not not_8 (not_8_out, IRQ7);
  PriorityEncoder #(.Selector_Bits(3)) priorityencoder_1 (
    .in0(not_1_out), .in1(not_2_out), .in2(not_3_out), .in3(not_4_out), .in4(not_5_out), .in5(not_6_out),
    .in6(not_7_out), .in7(not_8_out), .num({IPL2, IPL1, IPL0}));  // open: any
  _74138 _74138_2 (
    .pin1(FC0), .pin2(FC1), .pin3(FC2), .pin4(nAS), .pin5(1'b0), .pin6(1'b1), .pin7(_74138_1_pin5),
    .pin8(1'b0), .pin16(1'b1));  // open: pin9, pin10, pin11, pin12, pin13, pin14, pin15

  // Notes on the sheet:
  //   A1: pin 5
  //   A2: pin 6
  //   A3: pin 7
  //   nAS: pin 8
  //   FC0: pin 2
  //   FC1: pin 3
  //   FC2: pin 4
endmodule
