// Digital circuit irq_glue_logic_v2.dig as structural Verilog
module irq_glue_logic_v2 (
  input  A1,
  input  A2,
  input  A3,
  input  nAS,
  input  FC0,
  input  FC1,
  input  FC2,
  input  IRQ1,
  input  IRQ2,
  input  IRQ3,
  input  IRQ4,
  input  IRQ5,
  input  IRQ6,
  input  IRQ7,
  output nIACK5,
  output nIACK3,
  output nIACK4,
  output nIACK1,
  output nIACK2,
  output nIACK7,
  output nIACK6,
  output IPL0,
  output IPL1,
  output IPL2,
  output nIACK0
);

  wire and_1_out, and_2_out, decoder_1_out_0, decoder_1_out_1, decoder_1_out_2, decoder_1_out_3,
       decoder_1_out_4, decoder_1_out_5, decoder_1_out_6, decoder_1_out_7, not_1_out, not_2_out, not_3_out,
       not_4_out, not_5_out, not_6_out, not_7_out, not_8_out, not_9_out, notconnected_1_out;
  wire [2:0] and_4_out, priorityencoder_1_num;

  and and_1 (and_1_out, FC0, FC1, FC2);
  not not_1 (not_1_out, nAS);
  and and_2 (and_2_out, and_1_out, not_1_out);
  // NotConnected on notconnected_1_out
  and and_3 (and_4_out[0], and_2_out, A1);
  not not_2 (not_2_out, notconnected_1_out);
  not not_3 (not_3_out, IRQ1);
  not not_4 (not_4_out, IRQ2);
  not not_5 (not_5_out, IRQ3);
  not not_6 (not_6_out, IRQ4);
  not not_7 (not_7_out, IRQ5);
  not not_8 (not_8_out, IRQ6);
  not not_9 (not_9_out, IRQ7);
  PriorityEncoder #(.Selector_Bits(3)) priorityencoder_1 (
    .in0(not_2_out), .in1(not_3_out), .in2(not_4_out), .in3(not_5_out), .in4(not_6_out), .in5(not_7_out),
    .in6(not_8_out), .in7(not_9_out), .num(priorityencoder_1_num));  // open: any
  and and_4 (and_4_out[1], and_2_out, A2);
  and and_5 (and_4_out[2], and_2_out, A3);
  not not_10 (IPL0, priorityencoder_1_num[0]);
  not not_11 (IPL1, priorityencoder_1_num[1]);
  not not_12 (IPL2, priorityencoder_1_num[2]);
  Decoder #(.Selector_Bits(3)) decoder_1 (
    .sel(and_4_out), .out_0(decoder_1_out_0), .out_1(decoder_1_out_1), .out_2(decoder_1_out_2),
    .out_3(decoder_1_out_3), .out_4(decoder_1_out_4), .out_5(decoder_1_out_5), .out_6(decoder_1_out_6),
    .out_7(decoder_1_out_7));
  not not_13 (nIACK0, decoder_1_out_0);
  not not_14 (nIACK1, decoder_1_out_1);
  not not_15 (nIACK2, decoder_1_out_2);
  not not_16 (nIACK3, decoder_1_out_3);
  not not_17 (nIACK4, decoder_1_out_4);
  not not_18 (nIACK5, decoder_1_out_5);
  not not_19 (nIACK6, decoder_1_out_6);
  not not_20 (nIACK7, decoder_1_out_7);

  // Notes on the sheet:
  //   A1: pin 5
  //   A2: pin 6
  //   A3: pin 7
  //   nAS: pin 8
  //   FC0: pin 2
  //   FC1: pin 3
  //   FC2: pin 4
endmodule
