// Digital circuit memorydecoding.dig as structural Verilog
module memorydecoding (
  input  nUDS,
  input  nLDS,
  input  R_nW,
  input  nAS,
  input  A1,
  input  A2,
  input  A3,
  input  A4,
  input  A5,
  input  A6,
  input  A7,
  input  A8,
  input  A9,
  input  A10,
  input  A11,
  input  A12,
  input  A13,
  input  A14,
  input  A15,
  input  A16,
  input  A17,
  input  A18,
  input  A19,
  input  A20,
  input  A21,
  input  A22,
  input  A23,
  input  in_60,
  input  in_68,
  input  in_69,
  output UPPER_WRITE,
  output out_6,
  output UPPER_READ,
  output out_8,
  output LOWER_WRITE,
  output out_10,
  output LOWER_READ,
  output out_12,
  output D0,
  output D1,
  output D2,
  output D3,
  output D4,
  output D5,
  output D6,
  output D7,
  output D8,
  output D9,
  output D10,
  output D11,
  output D12,
  output D13,
  output D14,
  output D15,
  output CS_ROM,
  output CS_Bank_0,
  output CS_Bank_1,
  output CS_Bank_2,
  output CS_Bank_3,
  output CS_Bank_4,
  output CS_Bank_5,
  output CS_Bank_6,
  output CS_Bank_7,
  output CS_Bank_8,
  output CS_Bank_9,
  output CS_Bank_10,
  output CS_Bank_11,
  output CS_I_O_0,
  output CS_I_O_1,
  output CS_I_O_2
);

  _74139 _74139_1 (
    .pin1(nLDS), .pin2(nAS), .pin3(R_nW), .pin4(LOWER_WRITE), .pin5(out_10), .pin6(LOWER_READ),
    .pin7(out_12), .pin8(1'b0), .pin9(out_8), .pin10(UPPER_READ), .pin11(out_6), .pin12(UPPER_WRITE),
    .pin13(R_nW), .pin14(nAS), .pin15(nUDS), .pin16(1'b1));
  EEPROM #(.AddrBits(19), .isProgramMemory("true"), .Bits(8)) Lower_ROM__odd (
    .A({A19, A18, A17, A16, A15, A14, A13, A12, A11, A10, A9, A8, A7, A6, A5, A4, A3, A2, A1}), .CS(~CS_ROM),
    .WE(~1'b1), .OE(~LOWER_READ), .D({D7, D6, D5, D4, D3, D2, D1, D0}));
  EEPROM #(.AddrBits(19), .isProgramMemory("true"), .Bits(8)) Upper_ROM__even (
    .A({A19, A18, A17, A16, A15, A14, A13, A12, A11, A10, A9, A8, A7, A6, A5, A4, A3, A2, A1}), .CS(~CS_ROM),
    .WE(~1'b1), .OE(~UPPER_READ), .D({D15, D14, D13, D12, D11, D10, D9, D8}));
  RAMSinglePortSel #(.AddrBits(19), .isProgramMemory("true"), .Bits(8)) Bank_0_Lower (
    .A({A19, A18, A17, A16, A15, A14, A13, A12, A11, A10, A9, A8, A7, A6, A5, A4, A3, A2, A1}),
    .CS(~CS_Bank_0), .WE(~LOWER_WRITE), .OE(~LOWER_READ), .D({D7, D6, D5, D4, D3, D2, D1, D0}));
  RAMSinglePortSel #(.AddrBits(19), .isProgramMemory("true"), .Bits(8)) Bank_0_Upper (
    .A({A19, A18, A17, A16, A15, A14, A13, A12, A11, A10, A9, A8, A7, A6, A5, A4, A3, A2, A1}),
    .CS(~CS_Bank_0), .WE(~UPPER_WRITE), .OE(~UPPER_READ), .D({D15, D14, D13, D12, D11, D10, D9, D8}));
  _74138 _74138_1 (
    .pin1(A20), .pin2(A21), .pin3(A22), .pin4(A23), .pin5(nAS), .pin6(in_60), .pin7(CS_Bank_6), .pin8(1'b0),
    .pin9(CS_Bank_5), .pin10(CS_Bank_4), .pin11(CS_Bank_3), .pin12(CS_Bank_2), .pin13(CS_Bank_1),
    .pin14(CS_Bank_0), .pin15(CS_ROM), .pin16(1'b1));
  _74138 _74138_2 (
    .pin1(A20), .pin2(A21), .pin3(A22), .pin4(in_68), .pin5(in_69), .pin6(A23), .pin7(CS_I_O_2), .pin8(1'b0),
    .pin9(CS_I_O_1), .pin10(CS_I_O_0), .pin11(CS_Bank_11), .pin12(CS_Bank_10), .pin13(CS_Bank_9),
    .pin14(CS_Bank_8), .pin15(CS_Bank_7), .pin16(1'b1));
  RAMSinglePortSel #(.AddrBits(19), .Bits(8)) Bank_1_Lower (
    .A({A19, A18, A17, A16, A15, A14, A13, A12, A11, A10, A9, A8, A7, A6, A5, A4, A3, A2, A1}),
    .CS(~CS_Bank_1), .WE(~LOWER_WRITE), .OE(~LOWER_READ), .D({D7, D6, D5, D4, D3, D2, D1, D0}));
  RAMSinglePortSel #(.AddrBits(19), .Bits(8)) Bank_1_Upper (
    .A({A19, A18, A17, A16, A15, A14, A13, A12, A11, A10, A9, A8, A7, A6, A5, A4, A3, A2, A1}),
    .CS(~CS_Bank_1), .WE(~UPPER_WRITE), .OE(~UPPER_READ), .D({D15, D14, D13, D12, D11, D10, D9, D8}));
  RAMSinglePortSel #(.AddrBits(19), .Bits(8)) Bank_2_Lower (
    .A({A19, A18, A17, A16, A15, A14, A13, A12, A11, A10, A9, A8, A7, A6, A5, A4, A3, A2, A1}),
    .CS(~CS_Bank_2), .WE(~LOWER_WRITE), .OE(~LOWER_READ), .D({D7, D6, D5, D4, D3, D2, D1, D0}));
  RAMSinglePortSel #(.AddrBits(19), .Bits(8)) Bank_2_Upper (
    .A({A19, A18, A17, A16, A15, A14, A13, A12, A11, A10, A9, A8, A7, A6, A5, A4, A3, A2, A1}),
    .CS(~CS_Bank_2), .WE(~UPPER_WRITE), .OE(~UPPER_READ), .D({D15, D14, D13, D12, D11, D10, D9, D8}));
  RAMSinglePortSel #(.AddrBits(19), .Bits(8)) Bank_3_Lower (
    .A({A19, A18, A17, A16, A15, A14, A13, A12, A11, A10, A9, A8, A7, A6, A5, A4, A3, A2, A1}),
    .CS(~CS_Bank_3), .WE(~LOWER_WRITE), .OE(~LOWER_READ), .D({D7, D6, D5, D4, D3, D2, D1, D0}));
  RAMSinglePortSel #(.AddrBits(19), .Bits(8)) Bank_3_Upper (
    .A({A19, A18, A17, A16, A15, A14, A13, A12, A11, A10, A9, A8, A7, A6, A5, A4, A3, A2, A1}),
    .CS(~CS_Bank_3), .WE(~UPPER_WRITE), .OE(~UPPER_READ), .D({D15, D14, D13, D12, D11, D10, D9, D8}));

  // Notes on the sheet:
  //   in_60: default 1
  //   contents of Lower_ROM__odd (hex, n*v repeats v):
  //   8*1
  //   contents of Upper_ROM__even (hex, n*v repeats v):
  //   2,5*1,0,1
  //   Start (HEX)	End (HEX)	Area	Kbyte
  //   $00000000	$000FFFFF	ROM	1024
  //   $00100000	$001FFFFF	RAM	1024
  //   $00200000	$002FFFFF	RAM	1024
  //   $00300000	$003FFFFF	RAM	1024
  //   $00400000	$004FFFFF	RAM	1024
  //   $00500000	$005FFFFF	RAM	1024
  //   $00600000	$006FFFFF	RAM	1024
  //   $00700000	$007FFFFF	RAM	1024
  //   $00800000	$008FFFFF	RAM	1024
  //   $00900000	$009FFFFF	RAM	1024
  //   $00A00000	$00AFFFFF	RAM	1024
  //   $00B00000	$00BFFFFF	RAM	1024
  //   $00C00000	$00CFFFFF	RAM	1024
  //   $00D00000	$00D7FFFF	I/O	512
  //   $00D80000	$00DFFFFF	I/O	512
  //   $00E00000	$00E3FFFF	I/O	256
  //   $00E40000	$00E7FFFF	I/O	256
  //   $00E80000	$00E8FFFF	I/O	256
  //   $00EC0000	$00EFFFFF	I/O	256
  //   $00F00000	$00F1FFFF	I/O	128
  //   $00F20000	$00F3FFFF	I/O	128
  //   $00F40000	$00F5FFFF	I/O	128
  //   $00F60000	$00F7FFFF	I/O	128
  //   $00F80000	$00F8FFFF	I/O	64
  //   $00F90000	$00F9FFFF	I/O	64
  //   $00FA0000	$00FAFFFF	I/O	64
  //   $00FB0000	$00FBFFFF	I/O	64
  //   $00FC0000	$00FCFFFF	I/O	64
  //   $00FD0000	$00FDFFFF	I/O	64
  //   $00FE0000	$00FEFFFF	I/O	64
  //   $00FF0000	$00FFFFFF	I/O	64
endmodule
