// Digital circuit scratch.dig as structural Verilog
module scratch (
  input  Chip_A,
  input  Chip_B,
  input  nAS,
  input  E_clock,
  output Bus_Device,
  output nBERR
);

  wire _74175_1_pin3, _74175_1_pin7, _74175_1_pin10, not_1_out;

  PullUp pullup_1 (.out(Chip_A));
  not not_1 (not_1_out, nAS);
  _74175 _74175_1 (
    .pin1(not_1_out), .pin3(_74175_1_pin3), .pin4(not_1_out), .pin5(_74175_1_pin3), .pin7(_74175_1_pin7),
    .pin8(1'b0), .pin9(E_clock), .pin10(_74175_1_pin10), .pin12(_74175_1_pin7), .pin13(_74175_1_pin10),
    .pin14(nBERR), .pin16(1'b1));  // open: pin2, pin6, pin11, pin15

  assign Bus_Device = Chip_A;
  assign Chip_B = Chip_A;

  // Notes on the sheet:
  //   +5v
endmodule
